// Logisim project TRABALHO DE ARQUITETURA DE COMPUTADORES CC3MB.circ as structural Verilog: 13 circuits, main circuit main
module main (
  input  D,
  input  [3:0] A,
  input  [3:0] B,
  input  [2:0] \Operações ,
  output Overflow,
  output Overflow_2,
  output [3:0] S
);

  wire decoder_1_s0, decoder_1_s1, decoder_1_s2, decoder_1_s3, decoder_1_s4, decoder_1_s5, not_1_out;
  wire [3:0] add_4_1_out_5, buffer_5_s, or_4_bits_1_out_3, rot_d_1_abcd_2, rot_l_1_abcd_2, sub_4_1_out_5;

  Decoder decoder_1 (
    .in_1(\Operações ), .S0(decoder_1_s0), .S1(decoder_1_s1), .S2(decoder_1_s2), .S3(decoder_1_s3),
    .S4(decoder_1_s4), .S5(decoder_1_s5));  // open: S6, S7
  Buffer buffer_1 (.B(B), .Controle(decoder_1_s0), .S(S));
  ADD_4 add_4_1 (.in_1(A), .VAI_1(Overflow), .in_2(B), .VEM_1(1'b0), .out_5(add_4_1_out_5));
  Buffer buffer_2 (.B(add_4_1_out_5), .Controle(decoder_1_s1), .S(S));
  Sub_4 sub_4_1 (.Overflow(Overflow_2), .in_1(A), .in_2(B), .Vem_1(1'b0), .out_5(sub_4_1_out_5));
  Buffer buffer_3 (.B(sub_4_1_out_5), .Controle(decoder_1_s2), .S(S));
  OR_4_bits or_4_bits_1 (.in_2(A), .in_1(B), .out_3(or_4_bits_1_out_3));
  Buffer buffer_4 (.B(or_4_bits_1_out_3), .Controle(decoder_1_s3), .S(S));
  Buffer_invertido buffer_invertido_1 (.in_1(B), .in_2(decoder_1_s4), .out_3(S));
  not not_1 (not_1_out, D);
  Rot_D rot_d_1 (.abcd_2(rot_d_1_abcd_2), .ABCD(A), .AB(B[1:0]));
  Rot_L rot_l_1 (.abcd_2(rot_l_1_abcd_2), .ABCD(A), .AB(B[1:0]));
  Buffer buffer_5 (.B(rot_l_1_abcd_2), .Controle(not_1_out), .S(buffer_5_s));
  Buffer buffer_6 (.B(rot_d_1_abcd_2), .Controle(D), .S(buffer_5_s));
  Buffer buffer_7 (.B(buffer_5_s), .Controle(decoder_1_s5), .S(S));
endmodule

module ADD_1 (
  input  A,
  input  B,
  input  VEM_1,
  output S,
  output VAI_1
);

  wire and_1_out, and_2_out, or_1_out, xor_1_out;

  xor xor_1 (xor_1_out, A, B);
  or or_1 (or_1_out, B, VEM_1);
  and and_1 (and_1_out, B, VEM_1);
  xor xor_2 (S, xor_1_out, VEM_1);
  and and_2 (and_2_out, or_1_out, A);
  or or_2 (VAI_1, and_2_out, and_1_out);
endmodule

module ADD_4 (
  input  [3:0] in_1,
  input  [3:0] in_2,
  input  VEM_1,
  output VAI_1,
  output [3:0] out_5
);

  wire add_1_2_vai_1, add_1_3_vai_1, add_1_4_vai_1;

  ADD_1 add_1_1 (.A(in_1[3]), .B(in_2[3]), .VEM_1(add_1_2_vai_1), .S(out_5[3]), .VAI_1(VAI_1));
  ADD_1 add_1_2 (.A(in_1[2]), .B(in_2[2]), .VEM_1(add_1_3_vai_1), .S(out_5[2]), .VAI_1(add_1_2_vai_1));
  ADD_1 add_1_3 (.A(in_1[1]), .B(in_2[1]), .VEM_1(add_1_4_vai_1), .S(out_5[1]), .VAI_1(add_1_3_vai_1));
  ADD_1 add_1_4 (.A(in_1[0]), .B(in_2[0]), .VEM_1(VEM_1), .S(out_5[0]), .VAI_1(add_1_4_vai_1));
endmodule

module Sub_1 (
  input  A,
  input  B,
  input  VEM_1,
  output S,
  output VAI_1
);

  wire and_1_out, and_2_out, not_1_out, or_1_out, xor_1_out;

  not not_1 (not_1_out, A);
  xor xor_1 (xor_1_out, A, B);
  or or_1 (or_1_out, B, VEM_1);
  and and_1 (and_1_out, B, VEM_1);
  xor xor_2 (S, xor_1_out, VEM_1);
  and and_2 (and_2_out, or_1_out, not_1_out);
  or or_2 (VAI_1, and_2_out, and_1_out);
endmodule

module Sub_4 (
  input  [3:0] in_1,
  input  [3:0] in_2,
  input  Vem_1,
  output Overflow,
  output [3:0] out_5
);

  wire sub_1_2_vai_1, sub_1_3_vai_1, sub_1_4_vai_1;

  Sub_1 sub_1_1 (.A(in_1[3]), .B(in_2[3]), .VEM_1(sub_1_2_vai_1), .S(out_5[3]), .VAI_1(Overflow));
  Sub_1 sub_1_2 (.A(in_1[2]), .B(in_2[2]), .VEM_1(sub_1_3_vai_1), .S(out_5[2]), .VAI_1(sub_1_2_vai_1));
  Sub_1 sub_1_3 (.A(in_1[1]), .B(in_2[1]), .VEM_1(sub_1_4_vai_1), .S(out_5[1]), .VAI_1(sub_1_3_vai_1));
  Sub_1 sub_1_4 (.A(in_1[0]), .B(in_2[0]), .VEM_1(Vem_1), .S(out_5[0]), .VAI_1(sub_1_4_vai_1));
endmodule

module Buffer (
  input  [3:0] B,
  input  Controle,
  output [3:0] S
);

  assign S[3] = Controle ? B[3] : 1'bz;  // Controlled_Buffer controlled_buffer_1
  assign S[2] = Controle ? B[2] : 1'bz;  // Controlled_Buffer controlled_buffer_2
  assign S[1] = Controle ? B[1] : 1'bz;  // Controlled_Buffer controlled_buffer_3
  assign S[0] = Controle ? B[0] : 1'bz;  // Controlled_Buffer controlled_buffer_4
endmodule

module Decoder (
  input  [2:0] in_1,
  output S0,
  output S1,
  output S2,
  output S3,
  output S4,
  output S5,
  output S6,
  output S7
);

  wire not_1_out, not_2_out, not_3_out, not_4_out, not_5_out, not_6_out, not_7_out, not_8_out, not_9_out,
       not_10_out, not_11_out, not_12_out;

  not not_1 (not_1_out, in_1[2]);
  not not_2 (not_2_out, in_1[1]);
  and and_1 (S0, not_1_out, not_2_out, not_3_out);
  not not_3 (not_3_out, in_1[0]);
  not not_4 (not_4_out, in_1[2]);
  not not_5 (not_5_out, in_1[1]);
  and and_2 (S1, not_4_out, not_5_out, in_1[0]);
  not not_6 (not_6_out, in_1[2]);
  and and_3 (S2, not_6_out, in_1[1], not_7_out);
  not not_7 (not_7_out, in_1[0]);
  not not_8 (not_8_out, in_1[2]);
  and and_4 (S3, not_8_out, in_1[1], in_1[0]);
  and and_5 (S4, in_1[2], not_9_out, not_10_out);
  not not_9 (not_9_out, in_1[1]);
  not not_10 (not_10_out, in_1[0]);
  and and_6 (S5, in_1[2], not_11_out, in_1[0]);
  not not_11 (not_11_out, in_1[1]);
  and and_7 (S6, in_1[2], in_1[1], not_12_out);
  not not_12 (not_12_out, in_1[0]);
  and and_8 (S7, in_1[2], in_1[1], in_1[0]);
endmodule

module Buffer_invertido (
  input  [3:0] in_1,
  input  in_2,
  output [3:0] out_3
);

  assign out_3[3] = in_2 ? ~in_1[3] : 1'bz;  // Controlled_Inverter controlled_inverter_1
  assign out_3[1] = in_2 ? ~in_1[1] : 1'bz;  // Controlled_Inverter controlled_inverter_2
  assign out_3[2] = in_2 ? ~in_1[2] : 1'bz;  // Controlled_Inverter controlled_inverter_3
  assign out_3[0] = in_2 ? ~in_1[0] : 1'bz;  // Controlled_Inverter controlled_inverter_4
endmodule

module Rot_L (
  input  [3:0] ABCD,
  input  [1:0] AB,
  output [3:0] abcd_2
);

  wire and_1_out, and_2_out, and_3_out, and_4_out, and_5_out, and_6_out, and_7_out, and_8_out, and_9_out;

  and and_1 (and_1_out, ~AB[1], ~AB[0], ABCD[3]);  // AND_Gate
  and and_2 (and_2_out, ~AB[1], AB[0], ABCD[2]);  // AND_Gate
  and and_3 (and_3_out, AB[1], ~AB[0], ABCD[1]);  // AND_Gate
  and and_4 (and_4_out, AB[1], AB[0], ABCD[0]);
  and and_5 (and_5_out, ~AB[1], ~AB[0], ABCD[2]);  // AND_Gate
  and and_6 (and_6_out, ~AB[1], AB[0], ABCD[1]);  // AND_Gate
  and and_7 (and_7_out, AB[1], ~AB[0], ABCD[0]);  // AND_Gate
  and and_8 (and_8_out, ~AB[1], ~AB[0], ABCD[1]);  // AND_Gate
  and and_9 (and_9_out, ~AB[1], AB[0], ABCD[0]);  // AND_Gate
  and and_10 (abcd_2[0], ~AB[1], ~AB[0], ABCD[0]);  // AND_Gate
  or or_1 (abcd_2[3], and_1_out, and_2_out, and_3_out, and_4_out);
  or or_2 (abcd_2[2], and_5_out, and_6_out, and_7_out);
  or or_3 (abcd_2[1], and_8_out, and_9_out);
endmodule

module Rot_D (
  input  [3:0] ABCD,
  input  [1:0] AB,
  output [3:0] abcd_2
);

  wire and_1_out, and_2_out, and_3_out, and_4_out, and_5_out, and_6_out, and_7_out, and_8_out, and_9_out;

  and and_1 (and_1_out, ~AB[1], ~AB[0], ABCD[0]);  // AND_Gate
  and and_2 (and_2_out, ~AB[1], AB[0], ABCD[1]);  // AND_Gate
  and and_3 (and_3_out, AB[1], ~AB[0], ABCD[2]);  // AND_Gate
  and and_4 (and_4_out, AB[1], AB[0], ABCD[3]);
  and and_5 (and_5_out, ~AB[1], ~AB[0], ABCD[1]);  // AND_Gate
  and and_6 (and_6_out, ~AB[1], AB[0], ABCD[2]);  // AND_Gate
  and and_7 (and_7_out, AB[1], ~AB[0], ABCD[3]);  // AND_Gate
  and and_8 (and_8_out, ~AB[1], ~AB[0], ABCD[2]);  // AND_Gate
  and and_9 (and_9_out, ~AB[1], AB[0], ABCD[3]);  // AND_Gate
  and and_10 (abcd_2[3], ~AB[1], ~AB[0], ABCD[3]);  // AND_Gate
  or or_1 (abcd_2[0], and_1_out, and_2_out, and_3_out, and_4_out);
  or or_2 (abcd_2[1], and_5_out, and_6_out, and_7_out);
  or or_3 (abcd_2[2], and_8_out, and_9_out);
endmodule

module OR_4_bits (
  input  [3:0] in_1,
  input  [3:0] in_2,
  output [3:0] out_3
);

  or or_1 (out_3[3], in_2[3], in_1[3]);
  or or_2 (out_3[2], in_2[2], in_1[2]);
  or or_3 (out_3[1], in_2[1], in_1[1]);
  or or_4 (out_3[0], in_2[0], in_1[0]);
endmodule

module ULA (
  input  [3:0] Operando,
  input  [2:0] Upcode,
  input  E,
  output OVERFLOW,
  output Zero
);

  wire clock_1_out;
  wire [3:0] main_1_s, reg_ac_1_q;

  Clock clock_1 (.out(clock_1_out));
  // Probe on reg_ac_1_q
  main main_1 (
    .D(E), .A(reg_ac_1_q), .B(Operando), .Overflow(OVERFLOW), .Overflow_2(Zero), .\Operações (Upcode),
    .S(main_1_s));
  REG_AC reg_ac_1 (.D(main_1_s), .Q(reg_ac_1_q), .Clock(clock_1_out));
  // Probe on Operando
  // Probe on main_1_s
endmodule

module REG_AC (
  input  Clock,
  input  [3:0] D,
  output [3:0] Q
);

  D_Flip_Flop D3 (.clk(Clock), .D(D[3]), .Q(Q[3]));  // open: Qn, preset, en, reset
  D_Flip_Flop D2 (.clk(Clock), .D(D[2]), .Q(Q[2]));  // open: Qn, preset, en, reset
  D_Flip_Flop D1 (.clk(Clock), .D(D[1]), .Q(Q[1]));  // open: Qn, preset, en, reset
  D_Flip_Flop D0 (.clk(Clock), .D(D[0]), .Q(Q[0]));  // open: Qn, preset, en, reset
endmodule
